# Fritzing sketch USBComm (saved by Fritzing 0.8.3b)
circuit board: 3.68368cm x 5.33437cm
breadboards: 1

parts:
  JR = FTDI_BASIC [package=ftdi_basic]
  JL = FTDI_BASIC [package=ftdi_basic]
  USB = USB Connectors [package=usb-microb]
  FT232RL = USB UART [package=ssop28db]
  R/G_SWITCH = SWITCH-SP3T [package=switch-sp3t-smd]
  PWR_SWITCH = SWITCH-SP3T [package=switch-sp3t-smd]
  Pad1 = Pad [width=0.7 height=1.4 connect=center]
  Pad2 = Pad [width=0.7 height=1.4 connect=center]
  C1 = Capacitor Polarized [package=eia3528-kit]
  ISP = AVR ISP 6 Pin [package=2x3_offset]
  3V3 = Header 1 [package=1x01_offset]
  Fid1 = Pad [width=2.54 height=2.54 connect=center]  # not connected
  Fid2 = Pad [width=2.54 height=2.54 connect=center]  # not connected
  Fid3 = Pad [width=2.54 height=2.54 connect=center]  # not connected

nets:
  GND: JR.5, JL.5, USB.GND, FT232RL.GND7, FT232RL.GND18, FT232RL.GND21, FT232RL.AGND, FT232RL.TEST, Pad2.pad, C1.-, ISP.6
  N1: JR.1, JR.6, JL.6, PWR_SWITCH.1, C1.+, ISP.2
  N2: JR.2, R/G_SWITCH.1
  N3: JR.3, JL.3, FT232RL.TXD, ISP.3
  N4: JR.4, JL.4, FT232RL.RXD
  N5: JL.2, R/G_SWITCH.2
  N6: USB.D+, FT232RL.USBDP
  N7: USB.D-, FT232RL.USBDM
  N8: USB.VBUS, FT232RL.VCC, PWR_SWITCH.3, Pad1.pad
  N9: FT232RL.DTR, R/G_SWITCH.3, ISP.5
  N10: FT232RL.RTS, ISP.4
  N11: FT232RL.CTS, ISP.1
  N12: FT232RL.3V3OUT, PWR_SWITCH.2, 3V3.1

notes:
  5V GND RX  TX RST
  5V GND RX  TX RST VOUT
  RED
  GRN
  R/G SWITCH
  OUT
  GND MOSI VCC
  RST SCK MISO
  LEDgoes USB
  Communicator
